// Logisim project CPU.circ as structural Verilog: 36 circuits, main circuit main
// IF
module main (
  output [31:0] eax,
  output [31:0] ecx,
  output [31:0] edx,
  output [31:0] ebx,
  output [31:0] esp,
  output [31:0] ebp,
  output [31:0] esi,
  output [31:0] edi
);

  wire ccen_1_ccen, clock_1_out, cnd_1_cnd, control_hazard_handler_1_d_bubble,
       control_hazard_handler_1_d_stall, control_hazard_handler_1_e_bubble, control_hazard_handler_1_f_stall,
       ex_mem_1_cnd_2, global_count_1_clk_2, global_count_1_cntisfive, global_count_1_cntiszero, halt_1_halt,
       mem_sig_1_read, mem_sig_1_write;
  wire [2:0] alu_1_flgs, cc_1_flgs_2;
  wire [3:0] cmov_addr_handler_1_dste_2, dste_1_dste, dstm_1_dstm, ex_mem_1_dste_2, ex_mem_1_dstm_2,
       ex_mem_1_icode_2, fetch_unit_1_icode, fetch_unit_1_ifun, fetch_unit_1_length, fetch_unit_1_ra,
       fetch_unit_1_rb, global_count_1_cnt, halt_1_icode_2, id_ex_1_dste_2, id_ex_1_dstm_2, id_ex_1_icode_2,
       id_ex_1_ifun_2, if_id_1_icode_2, if_id_1_ifun_2, if_id_1_ra_2, if_id_1_rb_2, mem_wbn_1_dste_2,
       mem_wbn_1_dstm_2, mem_wbn_1_icode_2, srca_1_srca, srcb_1_srcb;
  wire [23:0] fetch_unit_1_pc_2, select_pc_1_pc;
  wire [31:0] alu_1_vale, alu_a_1_alu_a, alu_b_1_alu_b, data_memory_1_valm, decode_unit_1_vala,
       decode_unit_1_valb, ex_mem_1_vala_2, ex_mem_1_vale_2, fetch_unit_1_valc, forward_selecta_1_vala_2,
       forwardb_1_valb_2, id_ex_1_vala_2, id_ex_1_valb_2, id_ex_1_valc_2, if_1_out_5, if_id_1_valc_2,
       if_id_1_valp_2, mem_addr_1_valaddr, mem_wbn_1_vale_2, mem_wbn_1_valm_2, pc_increment_1_valp,
       predict_pc_1_pc;

  Control_Hazard_Handler control_hazard_handler_1 (
    .M_icode(ex_mem_1_icode_2), .E_Cnd(cnd_1_cnd), .E_icode(id_ex_1_icode_2), .E_dstM(id_ex_1_dstm_2),
    .E_bubble(control_hazard_handler_1_e_bubble), .D_icode(if_id_1_icode_2),
    .D_stall(control_hazard_handler_1_d_stall), .D_bubble(control_hazard_handler_1_d_bubble),
    .srcB(srcb_1_srcb), .srcA(srca_1_srca), .F_stall(control_hazard_handler_1_f_stall));
  Clock clock_1 (.out(clock_1_out));
  Halt halt_1 (
    .cntIsZero(global_count_1_cntisfive), .icode(mem_wbn_1_icode_2), .halt(halt_1_halt),
    .icode_2(halt_1_icode_2));
  Global_Count global_count_1 (
    .clk(clock_1_out), .clk_2(global_count_1_clk_2), .CntIsFive(global_count_1_cntisfive),
    .Cnt(global_count_1_cnt), .stop(halt_1_halt), .CntIsZero(global_count_1_cntiszero));
  MEM_WBN mem_wbn_1 (
    .cntIsFive(global_count_1_cntisfive), .clk(global_count_1_clk_2), .icode_2(mem_wbn_1_icode_2),
    .valE_2(mem_wbn_1_vale_2), .valM_2(mem_wbn_1_valm_2), .dstE_2(mem_wbn_1_dste_2),
    .dstM_2(mem_wbn_1_dstm_2), .icode(ex_mem_1_icode_2), .valE(ex_mem_1_vale_2), .valM(data_memory_1_valm),
    .dstE(ex_mem_1_dste_2), .dstM(ex_mem_1_dstm_2));
  EX_MEM ex_mem_1 (
    .cntIsFive(global_count_1_cntisfive), .clk(global_count_1_clk_2), .icode_2(ex_mem_1_icode_2),
    .Cnd_2(ex_mem_1_cnd_2), .valE_2(ex_mem_1_vale_2), .valA_2(ex_mem_1_vala_2), .dstE_2(ex_mem_1_dste_2),
    .dstM_2(ex_mem_1_dstm_2), .icode(id_ex_1_icode_2), .Cnd(cnd_1_cnd), .valE(alu_1_vale),
    .valA(id_ex_1_vala_2), .dstE(cmov_addr_handler_1_dste_2), .dstM(id_ex_1_dstm_2));
  Cnd cnd_1 (.Cnd(cnd_1_cnd), .ifun(id_ex_1_ifun_2), .Flgs(cc_1_flgs_2));
  CC cc_1 (.Flgs(alu_1_flgs), .Flgs_2(cc_1_flgs_2), .Clk(global_count_1_clk_2), .En(ccen_1_ccen));
  CCEn ccen_1 (.CCEn(ccen_1_ccen), .icode(id_ex_1_icode_2));
  ID_EX id_ex_1 (
    .cntIsFive(global_count_1_cntisfive), .bubble(control_hazard_handler_1_e_bubble),
    .clk(global_count_1_clk_2), .icode_2(id_ex_1_icode_2), .ifun_2(id_ex_1_ifun_2), .valC_2(id_ex_1_valc_2),
    .valA_2(id_ex_1_vala_2), .valB_2(id_ex_1_valb_2), .dstE_2(id_ex_1_dste_2), .dstM_2(id_ex_1_dstm_2),
    .icode(if_id_1_icode_2), .ifun(if_id_1_ifun_2), .valC(if_id_1_valc_2), .valA(forward_selecta_1_vala_2),
    .valB(forwardb_1_valb_2), .dstE(dste_1_dste), .dstM(dstm_1_dstm));
  IF_ID if_id_1 (
    .stall(control_hazard_handler_1_d_stall), .bubble(control_hazard_handler_1_d_bubble),
    .icode_2(if_id_1_icode_2), .ifun_2(if_id_1_ifun_2), .rA_2(if_id_1_ra_2), .rB_2(if_id_1_rb_2),
    .icode(fetch_unit_1_icode), .ifun(fetch_unit_1_ifun), .rA(fetch_unit_1_ra), .rB(fetch_unit_1_rb),
    .clk(global_count_1_clk_2), .cntIsFive(global_count_1_cntisfive), .valC_2(if_id_1_valc_2),
    .valP_2(if_id_1_valp_2), .valC(fetch_unit_1_valc), .valP(pc_increment_1_valp));
  Forward_SelectA forward_selecta_1 (
    .W_dstE(mem_wbn_1_dste_2), .W_valE(mem_wbn_1_vale_2), .W_dstM(mem_wbn_1_dstm_2),
    .W_valM(mem_wbn_1_valm_2), .M_dstE(ex_mem_1_dste_2), .M_valE(ex_mem_1_vale_2), .M_dstM(ex_mem_1_dstm_2),
    .M_valM(data_memory_1_valm), .E_dstE(cmov_addr_handler_1_dste_2), .E_valE(alu_1_vale),
    .icode(if_id_1_icode_2), .srcA(srca_1_srca), .valP(if_id_1_valp_2), .valA(decode_unit_1_vala),
    .valA_2(forward_selecta_1_vala_2));
  Select_PC select_pc_1 (
    .W_icode(halt_1_icode_2), .W_valM(mem_wbn_1_valm_2), .M_icode(ex_mem_1_icode_2), .M_Cnd(ex_mem_1_cnd_2),
    .M_valA(ex_mem_1_vala_2), .PC_pred(if_1_out_5), .PC(select_pc_1_pc));
  IF if_1 (
    .cntIsFive(global_count_1_cntisfive), .stall(control_hazard_handler_1_f_stall),
    .clk(global_count_1_clk_2), .PredPC(predict_pc_1_pc), .out_5(if_1_out_5));
  Mem__Sig mem_sig_1 (.icode(ex_mem_1_icode_2), .Write(mem_sig_1_write), .Read(mem_sig_1_read));
  Fetch_Unit fetch_unit_1 (
    .Cnt(global_count_1_cnt), .clk(global_count_1_clk_2), .PC_2(fetch_unit_1_pc_2),
    .Length(fetch_unit_1_length), .icode(fetch_unit_1_icode), .valC(fetch_unit_1_valc),
    .ifun(fetch_unit_1_ifun), .rA(fetch_unit_1_ra), .rB(fetch_unit_1_rb), .PC(select_pc_1_pc),
    .cntIsZero(global_count_1_cntiszero));
  Mem_Addr mem_addr_1 (
    .icode(ex_mem_1_icode_2), .valE(ex_mem_1_vale_2), .valA(ex_mem_1_vala_2), .valAddr(mem_addr_1_valaddr));
  ALU alu_1 (
    .Flgs(alu_1_flgs), .valE(alu_1_vale), .valA(alu_a_1_alu_a), .valB(alu_b_1_alu_b), .ifun(id_ex_1_ifun_2),
    .isOp(ccen_1_ccen));
  ALU_A alu_a_1 (.ALU_A(alu_a_1_alu_a), .icode(id_ex_1_icode_2), .valA(id_ex_1_vala_2), .valC(id_ex_1_valc_2));
  ALU_B alu_b_1 (.ALU_B(alu_b_1_alu_b), .icode(id_ex_1_icode_2), .valB(id_ex_1_valb_2));
  ForwardB forwardb_1 (
    .W_dstE(mem_wbn_1_dste_2), .W_valE(mem_wbn_1_vale_2), .W_dstM(mem_wbn_1_dstm_2),
    .W_valM(mem_wbn_1_valm_2), .M_dstE(ex_mem_1_dste_2), .M_valE(ex_mem_1_vale_2), .M_dstM(ex_mem_1_dstm_2),
    .M_valM(data_memory_1_valm), .E_dstE(cmov_addr_handler_1_dste_2), .E_valE(alu_1_vale),
    .valB(decode_unit_1_valb), .srcB(srcb_1_srcb), .valB_2(forwardb_1_valb_2));
  Predict_PC predict_pc_1 (
    .icode(fetch_unit_1_icode), .valP(pc_increment_1_valp), .valC(fetch_unit_1_valc), .PC(predict_pc_1_pc));
  PC_Increment pc_increment_1 (.Old_PC(fetch_unit_1_pc_2), .OpLen(fetch_unit_1_length), .valP(pc_increment_1_valp));
  Data_Memory data_memory_1 (
    .write(mem_sig_1_write), .read(mem_sig_1_read), .clk(global_count_1_clk_2), .valM(data_memory_1_valm),
    .valAddr(mem_addr_1_valaddr), .valA(ex_mem_1_vala_2), .count(global_count_1_cnt));
  srcA srca_1 (.srcA(srca_1_srca), .icode(if_id_1_icode_2), .rA(if_id_1_ra_2));
  srcB srcb_1 (.srcB(srcb_1_srcb), .icode(if_id_1_icode_2), .rB(if_id_1_rb_2));
  cmov_Addr_Handler cmov_addr_handler_1 (
    .icode(id_ex_1_icode_2), .Cnd(cnd_1_cnd), .dstE_2(cmov_addr_handler_1_dste_2), .dstE(id_ex_1_dste_2));
  Decode_Unit decode_unit_1 (
    .clk(global_count_1_clk_2), .valE(mem_wbn_1_vale_2), .dstE(mem_wbn_1_dste_2), .valM(mem_wbn_1_valm_2),
    .dstM(mem_wbn_1_dstm_2), .valA(decode_unit_1_vala), .valB(decode_unit_1_valb), .srcA(srca_1_srca),
    .srcB(srcb_1_srcb), .eax(eax), .ecx(ecx), .edx(edx), .ebx(ebx), .esp(esp), .ebp(ebp), .esi(esi), .edi(edi));
  dstE dste_1 (.dstE(dste_1_dste), .icode(if_id_1_icode_2), .rB(if_id_1_rb_2));
  dstM dstm_1 (.dstM(dstm_1_dstm), .icode(if_id_1_icode_2), .rA(if_id_1_ra_2));
endmodule

// Cnt
module Global_Count (
  input  stop,
  input  clk,
  output [3:0] Cnt,
  output CntIsFive,
  output CntIsZero,
  output clk_2
);

  wire and_1_out, d_ff_1_q, d_ff_1_qn, nor_1_out;

  D_Flip_Flop d_ff_1 (.clk(and_1_out), .D(d_ff_1_qn), .Q(d_ff_1_q), .Qn(d_ff_1_qn));  // open: preset, en, reset
  and and_1 (and_1_out, d_ff_1_qn, clk);
  Counter #(.width(4), .max('h5)) u_Cnt (.count(d_ff_1_q), .Q(Cnt), .clk(clk), .clr(stop));  // open: load, D, carry
  and and_2 (CntIsFive, Cnt[0], ~Cnt[1], Cnt[2]);  // AND_Gate
  nor nor_1 (nor_1_out, Cnt[0], Cnt[1], Cnt[2]);
  and and_3 (CntIsZero, nor_1_out, d_ff_1_q);
  Multiplexer #(.enable("false")) multiplexer_1 (.in0(clk), .in1(1'b0), .out(clk_2), .sel(stop));
endmodule

module IF (
  input  cntIsFive,
  input  stall,
  input  clk,
  input  [31:0] PredPC,
  output [31:0] out_5
);

  wire and_1_out;
  wire [31:0] register_1_q;

  and and_1 (and_1_out, cntIsFive, ~stall);  // AND_Gate
  Register #(.width(32)) register_1 (.D(PredPC), .Q(register_1_q), .clk(clk));  // open: en, clr
  Register #(.width(32), .trigger("falling")) register_2 (
    .D(register_1_q), .Q(out_5), .clk(and_1_out));  // open: en, clr
endmodule

module Select_PC (
  input  [3:0] W_icode,
  input  [31:0] W_valM,
  input  [3:0] M_icode,
  input  M_Cnd,
  input  [31:0] PC_pred,
  input  [31:0] M_valA,
  output [23:0] PC
);

  wire and_1_out, and_2_out, and_3_out, and_4_out, nor_1_out;
  wire [7:0] controlled_buffer_1_out;

  assign {controlled_buffer_1_out, PC} = nor_1_out ? PC_pred : 32'bz;  // Controlled_Buffer controlled_buffer_1
  nor nor_1 (nor_1_out, and_1_out, and_3_out);
  assign {controlled_buffer_1_out, PC} = and_1_out ? W_valM : 32'bz;  // Controlled_Buffer controlled_buffer_2
  assign {controlled_buffer_1_out, PC} = and_3_out ? M_valA : 32'bz;  // Controlled_Buffer controlled_buffer_3
  and and_1 (and_1_out, W_icode[0], ~W_icode[1], ~W_icode[2], W_icode[3], ~and_3_out);  // AND_Gate
  and and_2 (and_2_out, and_4_out, ~M_icode[3]);  // AND_Gate
  and and_3 (and_3_out, and_2_out, ~M_Cnd);  // AND_Gate
  and and_4 (and_4_out, M_icode[0], M_icode[1], M_icode[2]);
endmodule

// Instruction Memory
module Fetch_Unit (
  input  [23:0] PC,
  input  cntIsZero,
  input  [3:0] Cnt,
  input  clk,
  output [23:0] PC_2,
  output [3:0] icode,
  output [3:0] ifun,
  output [3:0] rA,
  output [3:0] rB,
  output [3:0] Length,
  output [31:0] valC
);

  wire and_1_out, and_2_out, and_3_out, and_4_out, comparator_1_gt, not_1_out, or_1_out, or_2_out, or_3_out;
  wire [1:0] multiplexer_3_out, valc_buffer_handler_1_out_2, valc_buffer_handler_2_out_2;
  wire [3:0] adder_2_out, multiplexer_1_out, multiplexer_2_out, register_2_q, rom_1_data, rom_1_data_2;
  wire [7:0] demultiplexer_1_out0, demultiplexer_1_out1;
  wire [23:0] adder_1_out, bit_extender_1_out;

  Register #(.width(4)) register_1 (.D(register_2_q), .en(cntIsZero), .Q(Length), .clk(clk));  // open: clr
  Comparator #(.width(4)) comparator_1 (.a(Length), .b(Cnt), .gt(comparator_1_gt));  // open: eq, lt
  Multiplexer #(.select(4), .width(4), .disabled(0), .enable("false")) multiplexer_1 (
    .in0(4'b0001), .in1(4'b0001), .in2(4'b0010), .in3(4'b0110), .in4(4'b0110), .in5(4'b0110), .in6(4'b0010),
    .in7(4'b0101), .in8(4'b0101), .in9(4'b0001), .in10(4'b0010), .in11(4'b0010), .out(multiplexer_1_out),
    .sel(rom_1_data_2));  // open: in12, in13, in14, in15
  Multiplexer #(.width(4), .enable("false")) multiplexer_2 (
    .in0(Length), .in1(Cnt), .out(multiplexer_2_out), .sel(comparator_1_gt));
  Register #(.width(4), .trigger("high")) register_2 (
    .D(multiplexer_1_out), .Q(register_2_q), .clk(and_4_out));  // open: en, clr
  assign bit_extender_1_out = {{20{1'b0}}, multiplexer_2_out};  // Bit_Extender bit_extender_1
  Adder #(.width(24)) adder_1 (.a(PC), .b(bit_extender_1_out), .out(adder_1_out));  // open: cin, cout
  or or_1 (or_1_out, multiplexer_2_out[1], multiplexer_2_out[2], multiplexer_2_out[3]);
  valC_Buffer_Handler valc_buffer_handler_1 (.in_1(multiplexer_2_out), .out_2(valc_buffer_handler_1_out_2));
  Adder #(.width(4)) adder_2 (.a(multiplexer_2_out), .b(4'b0000), .out(adder_2_out), .cin(1'b1));  // open: cout
  and and_1 (and_1_out, icode[3], ~icode[2], ~icode[1], ~icode[0]);  // AND_Gate
  ROM #(.addrWidth(24)) rom_1 (.addr(adder_1_out), .data({rom_1_data_2, rom_1_data}));  // open: sel
  and and_2 (and_2_out, multiplexer_2_out[0], or_2_out);
  Multiplexer #(.width(2), .disabled(0), .enable("false")) multiplexer_3 (
    .in0(valc_buffer_handler_1_out_2), .in1(valc_buffer_handler_2_out_2), .out(multiplexer_3_out),
    .sel(or_2_out));
  valC_Buffer_Handler valc_buffer_handler_2 (.in_1(adder_2_out), .out_2(valc_buffer_handler_2_out_2));
  and and_3 (and_3_out, ~icode[3], icode[2], icode[1], icode[0]);  // AND_Gate
  or or_2 (or_2_out, and_1_out, and_3_out);
  Demultiplexer #(.width(8), .disabled(0), .enable("false")) demultiplexer_1 (
    .out0(demultiplexer_1_out0), .out1(demultiplexer_1_out1), .in({rom_1_data_2, rom_1_data}), .sel(or_3_out));
  or or_3 (or_3_out, and_2_out, or_1_out);
  and and_4 (and_4_out, ~multiplexer_2_out[0], not_1_out);  // AND_Gate
  not not_1 (not_1_out, or_3_out);
  _2_2_x4_RFile u_2_2_x4_rfile_1 (
    .Address(multiplexer_2_out[0]), .Enable(not_1_out), .I_DATA(demultiplexer_1_out0), .CLK(clk),
    .icode(icode), .ifun(ifun), .rA(rA), .rB(rB));
  _4x8_RFile u_4x8_rfile_1 (
    .En(comparator_1_gt), .Address(multiplexer_3_out), .I_DATA(demultiplexer_1_out1), .CLK(clk),
    .Bits_0_7(valC[7:0]), .Bits_8_15(valC[15:8]), .Bits_16_23(valC[23:16]), .Bits_24_31(valC[31:24]));

  assign PC_2 = PC;

  // Notes on the sheet:
  //   Size MUX
  //   contents of rom_1 (hex, n*v repeats v):
  //   30 f4 0 2 0 0 30 f5 0 2 0 0 70 2c 6*0 1 4*0 ff ff ff 10 6*0 ff 0 10 0 0 4*ff 80 32 4*0 a0 5f 20 45
  //   30 f7 14 0 0 0 30 f2 4*0 30 f6 4 0 0 0 70 73 0 0 0 a0 5f 20 45 20 23 60 62 50 12 14 0 0 0 a0 f 61 10
  //   b0 f 26 10 26 23 a0 7f 61 27 b0 7f 76 53 0 0 0 b0 5f 90 a0 2f 50 2 14 0 0 0 80 4d 0 0 0 b0 2f 50 12
  //   14 0 0 0 40 2 14 0 0 0 40 13 14 0 0 0 60 62 30 f3 14 0 0 0 61 23 30 f3 14 0 0 0 76 73 0 0 0 b0 5f 90
endmodule

// Spl. Buf
module _2_2_x4_RFile (
  input  Address,
  input  Enable,
  input  [7:0] I_DATA,
  input  CLK,
  output [3:0] icode,
  output [3:0] ifun,
  output [3:0] rA,
  output [3:0] rB
);

  wire and_1_out, and_2_out, decoder_1_out0, decoder_1_out1;

  Decoder #(.disabled(0), .enable("false")) decoder_1 (.out0(decoder_1_out0), .out1(decoder_1_out1), .sel(Address));
  and and_1 (and_1_out, Enable, decoder_1_out0);
  and and_2 (and_2_out, decoder_1_out1, Enable);
  Register #(.width(4), .trigger("falling")) register_1 (
    .D(I_DATA[7:4]), .en(and_1_out), .Q(icode), .clk(CLK));  // open: clr
  Register #(.width(4), .trigger("falling")) register_2 (
    .D(I_DATA[3:0]), .en(and_1_out), .Q(ifun), .clk(CLK));  // open: clr
  Register #(.width(4), .trigger("falling")) register_3 (
    .D(I_DATA[7:4]), .en(and_2_out), .Q(rA), .clk(CLK));  // open: clr
  Register #(.width(4), .trigger("falling")) register_4 (
    .D(I_DATA[3:0]), .en(and_2_out), .Q(rB), .clk(CLK));  // open: clr
endmodule

// 4B Buf
module _4x8_RFile (
  input  En,
  input  [1:0] Address,
  input  [7:0] I_DATA,
  input  CLK,
  output [7:0] Bits_0_7,
  output [7:0] Bits_8_15,
  output [7:0] Bits_16_23,
  output [7:0] Bits_24_31
);

  wire decoder_1_out0, decoder_1_out1, decoder_1_out2, decoder_1_out3;

  Decoder #(.select(2), .disabled(0)) decoder_1 (
    .out0(decoder_1_out0), .out1(decoder_1_out1), .out2(decoder_1_out2), .out3(decoder_1_out3),
    .sel(Address), .en(En));
  Register #(.trigger("falling")) register_1 (.D(I_DATA), .en(decoder_1_out0), .Q(Bits_0_7), .clk(CLK));  // open: clr
  Register #(.trigger("falling")) register_2 (.D(I_DATA), .en(decoder_1_out1), .Q(Bits_8_15), .clk(CLK));  // open: clr
  Register #(.trigger("falling")) register_3 (.D(I_DATA), .en(decoder_1_out2), .Q(Bits_16_23), .clk(CLK));  // open: clr
  Register #(.trigger("falling")) register_4 (.D(I_DATA), .en(decoder_1_out3), .Q(Bits_24_31), .clk(CLK));  // open: clr
endmodule

module valC_Buffer_Handler (
  input  [3:0] in_1,
  output [1:0] out_2
);

  not not_1 (out_2[1], in_1[1]);

  assign out_2[0] = in_1[0];
endmodule

// PC++
module PC_Increment (
  input  [23:0] Old_PC,
  input  [3:0] OpLen,
  output [31:0] valP
);

  wire [23:0] adder_1_out, bit_extender_1_out;

  assign bit_extender_1_out = {{20{1'b0}}, OpLen};  // Bit_Extender bit_extender_1
  Adder #(.width(24)) adder_1 (.a(Old_PC), .b(bit_extender_1_out), .out(adder_1_out), .cin(1'b0));  // open: cout
  assign valP = {{8{1'b0}}, adder_1_out};  // Bit_Extender bit_extender_2
endmodule

// Pred
module Predict_PC (
  input  [3:0] icode,
  input  [31:0] valP,
  input  [31:0] valC,
  output [31:0] PC
);

  wire and_1_out, and_2_out, nor_1_out, or_1_out;

  and and_1 (and_1_out, icode[0], icode[1], icode[2], ~icode[3]);  // AND_Gate
  nor nor_1 (nor_1_out, icode[0], icode[1], icode[2]);
  and and_2 (and_2_out, nor_1_out, icode[3]);
  or or_1 (or_1_out, and_1_out, and_2_out);
  Multiplexer #(.width(32), .enable("false")) multiplexer_1 (.in0(valP), .in1(valC), .out(PC), .sel(or_1_out));
endmodule

module IF_ID (
  input  cntIsFive,
  input  stall,
  input  bubble,
  input  clk,
  input  [3:0] icode,
  input  [3:0] ifun,
  input  [3:0] rA,
  input  [3:0] rB,
  input  [31:0] valC,
  input  [31:0] valP,
  output [3:0] icode_2,
  output [3:0] ifun_2,
  output [3:0] rA_2,
  output [3:0] rB_2,
  output [31:0] valC_2,
  output [31:0] valP_2
);

  wire and_1_out, not_1_out;
  wire [3:0] multiplexer_1_out, multiplexer_2_out, multiplexer_3_out, multiplexer_4_out;
  wire [31:0] register_6_q;

  not not_1 (not_1_out, stall);
  and and_1 (and_1_out, cntIsFive, not_1_out);
  Multiplexer #(.width(4), .enable("false")) multiplexer_1 (
    .in0(icode), .in1(4'b0001), .out(multiplexer_1_out), .sel(bubble));
  Register #(.width(4)) register_1 (.D(multiplexer_1_out), .en(and_1_out), .Q(icode_2), .clk(clk));  // open: clr
  Register #(.width(4)) register_2 (.D(multiplexer_2_out), .en(and_1_out), .Q(ifun_2), .clk(clk));  // open: clr
  Multiplexer #(.width(4), .enable("false")) multiplexer_2 (
    .in0(ifun), .in1(4'b0001), .out(multiplexer_2_out), .sel(bubble));
  Multiplexer #(.width(4), .enable("false")) multiplexer_3 (
    .in0(rA), .in1(4'b1111), .out(multiplexer_3_out), .sel(bubble));
  Register #(.width(4)) register_3 (.D(multiplexer_3_out), .en(and_1_out), .Q(rA_2), .clk(clk));  // open: clr
  Multiplexer #(.width(4), .enable("false")) multiplexer_4 (
    .in0(rB), .in1(4'b1111), .out(multiplexer_4_out), .sel(bubble));
  Register #(.width(4)) register_4 (.D(multiplexer_4_out), .en(and_1_out), .Q(rB_2), .clk(clk));  // open: clr
  Register #(.width(32)) register_5 (.D(valC), .en(and_1_out), .Q(valC_2), .clk(clk));  // open: clr
  Register #(.width(32)) register_6 (.D(valP), .Q(register_6_q), .clk(clk));  // open: en, clr
  Register #(.width(32)) register_7 (.D(register_6_q), .en(and_1_out), .Q(valP_2), .clk(clk));  // open: clr
endmodule

// Register File
module Decode_Unit (
  input  [31:0] valE,
  input  [3:0] dstE,
  input  [31:0] valM,
  input  [3:0] dstM,
  input  [3:0] srcA,
  input  [3:0] srcB,
  input  clk,
  output [31:0] eax,
  output [31:0] valA,
  output [31:0] valB,
  output [31:0] ecx,
  output [31:0] edx,
  output [31:0] ebx,
  output [31:0] esp,
  output [31:0] ebp,
  output [31:0] esi,
  output [31:0] edi
);

  Register_File register_file_1 (
    .clk(clk), .valE(valE), .valM(valM), .dstE(dstE), .dstM(dstM), .valA(valA), .valB(valB), .srcA(srcA),
    .srcB(srcB), .eax(eax), .ecx(ecx), .edx(edx), .ebx(ebx), .esp(esp), .ebp(ebp), .esi(esi), .edi(edi));
endmodule

// Fwd + Sel A
module Forward_SelectA (
  input  [3:0] W_dstE,
  input  [31:0] W_valE,
  input  [3:0] W_dstM,
  input  [31:0] W_valM,
  input  [3:0] M_dstE,
  input  [31:0] M_valE,
  input  [3:0] M_dstM,
  input  [31:0] M_valM,
  input  [3:0] E_dstE,
  input  [31:0] E_valE,
  input  [3:0] icode,
  input  [3:0] srcA,
  input  [31:0] valP,
  input  [31:0] valA,
  output [31:0] valA_2
);

  wire and_1_out, and_2_out, and_3_out, and_4_out, and_5_out, and_6_out, and_7_out, and_8_out, and_9_out,
       and_10_out, and_11_out, and_12_out, nor_1_out, nor_2_out, not_1_out, or_1_out, or_2_out, or_3_out,
       or_4_out;
  wire [3:0] xnor_1_out, xnor_2_out, xnor_3_out, xnor_4_out, xnor_5_out;

  and and_1 (and_1_out, ~icode[3], icode[2], icode[1], icode[0]);  // AND_Gate
  and and_2 (and_2_out, icode[3], nor_1_out);
  nor nor_1 (nor_1_out, icode[2], icode[1], icode[0]);
  or or_1 (or_1_out, and_1_out, and_2_out);
  assign valA_2 = or_1_out ? valP : 32'bz;  // Controlled_Buffer controlled_buffer_1
  assign valA_2 = nor_2_out ? valA : 32'bz;  // Controlled_Buffer controlled_buffer_2
  nor nor_2 (nor_2_out, and_5_out, and_3_out, and_4_out, and_6_out, and_7_out, or_1_out);
  assign valA_2 = and_3_out ? W_valE : 32'bz;  // Controlled_Buffer controlled_buffer_3
  and and_3 (and_3_out, and_8_out, ~srcA[3], ~or_2_out);  // AND_Gate
  assign valA_2 = and_4_out ? W_valM : 32'bz;  // Controlled_Buffer controlled_buffer_4
  and and_4 (and_4_out, and_9_out, ~srcA[3], ~or_3_out);  // AND_Gate
  assign valA_2 = and_5_out ? M_valE : 32'bz;  // Controlled_Buffer controlled_buffer_5
  and and_5 (and_5_out, and_10_out, ~srcA[3], ~or_4_out);  // AND_Gate
  assign valA_2 = and_6_out ? M_valM : 32'bz;  // Controlled_Buffer controlled_buffer_6
  and and_6 (and_6_out, and_11_out, ~srcA[3], ~and_12_out);  // AND_Gate
  assign valA_2 = and_7_out ? E_valE : 32'bz;  // Controlled_Buffer controlled_buffer_7
  and and_7 (and_7_out, and_12_out, ~srcA[3]);  // AND_Gate
  not not_1 (not_1_out, or_1_out);
  and and_8 (and_8_out, xnor_1_out[0], xnor_1_out[1], xnor_1_out[2], xnor_1_out[3], not_1_out);
  or or_2 (or_2_out, and_9_out, or_3_out);
  and and_9 (and_9_out, xnor_2_out[0], xnor_2_out[1], xnor_2_out[2], xnor_2_out[3], not_1_out);
  or or_3 (or_3_out, and_10_out, or_4_out);
  and and_10 (and_10_out, xnor_3_out[0], xnor_3_out[1], xnor_3_out[2], xnor_3_out[3], not_1_out);
  or or_4 (or_4_out, and_11_out, and_12_out);
  and and_11 (and_11_out, xnor_4_out[0], xnor_4_out[1], xnor_4_out[2], xnor_4_out[3], not_1_out);
  and and_12 (and_12_out, xnor_5_out[0], xnor_5_out[1], xnor_5_out[2], xnor_5_out[3], not_1_out);
  assign xnor_1_out = ~(W_dstE ^ srcA);  // XNOR_Gate xnor_1, 4 bits wide
  assign xnor_2_out = ~(W_dstM ^ srcA);  // XNOR_Gate xnor_2, 4 bits wide
  assign xnor_3_out = ~(M_dstE ^ srcA);  // XNOR_Gate xnor_3, 4 bits wide
  assign xnor_4_out = ~(M_dstM ^ srcA);  // XNOR_Gate xnor_4, 4 bits wide
  assign xnor_5_out = ~(E_dstE ^ srcA);  // XNOR_Gate xnor_5, 4 bits wide
endmodule

// Fwd B
module ForwardB (
  input  [3:0] W_dstE,
  input  [31:0] W_valE,
  input  [3:0] W_dstM,
  input  [31:0] W_valM,
  input  [3:0] M_dstE,
  input  [31:0] M_valE,
  input  [3:0] M_dstM,
  input  [31:0] M_valM,
  input  [3:0] E_dstE,
  input  [31:0] E_valE,
  input  [3:0] srcB,
  input  [31:0] valB,
  output [31:0] valB_2
);

  wire and_1_out, and_2_out, and_3_out, and_4_out, and_5_out, and_6_out, and_7_out, and_8_out, and_9_out,
       and_10_out, nor_1_out, or_1_out, or_2_out, or_3_out;
  wire [3:0] xnor_1_out, xnor_2_out, xnor_3_out, xnor_4_out, xnor_5_out;

  assign valB_2 = nor_1_out ? valB : 32'bz;  // Controlled_Buffer controlled_buffer_1
  nor nor_1 (nor_1_out, and_1_out, and_2_out, and_3_out, and_4_out, and_5_out);
  assign valB_2 = and_1_out ? W_valE : 32'bz;  // Controlled_Buffer controlled_buffer_2
  assign valB_2 = and_2_out ? W_valM : 32'bz;  // Controlled_Buffer controlled_buffer_3
  assign valB_2 = and_3_out ? M_valE : 32'bz;  // Controlled_Buffer controlled_buffer_4
  assign valB_2 = and_4_out ? M_valM : 32'bz;  // Controlled_Buffer controlled_buffer_5
  assign valB_2 = and_5_out ? E_valE : 32'bz;  // Controlled_Buffer controlled_buffer_6
  and and_1 (and_1_out, and_6_out, ~srcB[3], ~or_1_out);  // AND_Gate
  or or_1 (or_1_out, and_7_out, or_2_out);
  and and_2 (and_2_out, and_7_out, ~srcB[3], ~or_2_out);  // AND_Gate
  or or_2 (or_2_out, and_8_out, or_3_out);
  and and_3 (and_3_out, and_8_out, ~srcB[3], ~or_3_out);  // AND_Gate
  or or_3 (or_3_out, and_9_out, and_10_out);
  and and_4 (and_4_out, and_9_out, ~srcB[3], ~and_10_out);  // AND_Gate
  and and_5 (and_5_out, and_10_out, ~srcB[3]);  // AND_Gate
  and and_6 (and_6_out, xnor_1_out[0], xnor_1_out[1], xnor_1_out[2], xnor_1_out[3]);
  and and_7 (and_7_out, xnor_2_out[0], xnor_2_out[1], xnor_2_out[2], xnor_2_out[3]);
  and and_8 (and_8_out, xnor_3_out[0], xnor_3_out[1], xnor_3_out[2], xnor_3_out[3]);
  and and_9 (and_9_out, xnor_4_out[0], xnor_4_out[1], xnor_4_out[2], xnor_4_out[3]);
  and and_10 (and_10_out, xnor_5_out[0], xnor_5_out[1], xnor_5_out[2], xnor_5_out[3]);
  assign xnor_1_out = ~(W_dstE ^ srcB);  // XNOR_Gate xnor_1, 4 bits wide
  assign xnor_2_out = ~(W_dstM ^ srcB);  // XNOR_Gate xnor_2, 4 bits wide
  assign xnor_3_out = ~(M_dstE ^ srcB);  // XNOR_Gate xnor_3, 4 bits wide
  assign xnor_4_out = ~(M_dstM ^ srcB);  // XNOR_Gate xnor_4, 4 bits wide
  assign xnor_5_out = ~(E_dstE ^ srcB);  // XNOR_Gate xnor_5, 4 bits wide
endmodule

module srcA (
  input  [3:0] icode,
  input  [3:0] rA,
  output [3:0] srcA
);

  wire and_1_out, and_2_out, and_3_out;
  wire [1:0] or_1_out;

  and and_1 (and_1_out, ~icode[2], icode[0]);  // AND_Gate
  and and_2 (and_2_out, ~icode[2], ~icode[1]);  // AND_Gate
  and and_3 (and_3_out, icode[1], icode[0], ~icode[3]);  // AND_Gate
  and and_4 (or_1_out[1], icode[0], ~icode[2], icode[3]);  // AND_Gate
  or or_1 (or_1_out[0], and_1_out, and_2_out, and_3_out);
  Multiplexer #(.select(2), .width(4), .enable("false")) multiplexer_1 (
    .in0(rA), .in1(4'b1111), .in2(4'b0100), .in3(4'b0100), .out(srcA), .sel(or_1_out));
endmodule

module srcB (
  input  [3:0] icode,
  input  [3:0] rB,
  output [3:0] srcB
);

  wire nand_1_out;
  wire [0:0] and_1_out;

  nand nand_1 (nand_1_out, icode[0], icode[1]);
  and and_1 (and_1_out[0], nand_1_out, icode[2]);
  Multiplexer #(.select(2), .width(4), .enable("false")) multiplexer_1 (
    .in0(4'b1111), .in1(rB), .in2(4'b0100), .in3(4'b0100), .out(srcB), .sel({icode[3], and_1_out[0]}));
endmodule

module dstE (
  input  [3:0] icode,
  input  [3:0] rB,
  output [3:0] dstE
);

  wire and_1_out;
  wire [0:0] and_2_out;

  and and_1 (and_1_out, icode[0], icode[2]);
  and and_2 (and_2_out[0], ~and_1_out, icode[1]);  // AND_Gate
  Multiplexer #(.select(2), .width(4), .enable("false")) multiplexer_1 (
    .in0(4'b1111), .in1(rB), .in2(4'b0100), .in3(4'b0100), .out(dstE), .sel({icode[3], and_2_out[0]}));
endmodule

module dstM (
  input  [3:0] rA,
  input  [3:0] icode,
  output [3:0] dstM
);

  wire and_1_out, xor_1_out, xor_2_out;

  xor xor_1 (xor_1_out, icode[1], icode[2]);
  xor xor_2 (xor_2_out, icode[2], icode[3]);
  and and_1 (and_1_out, icode[0], xor_1_out, xor_2_out);
  Multiplexer #(.width(4), .enable("false")) multiplexer_1 (.in0(4'b1111), .in1(rA), .out(dstM), .sel(and_1_out));
endmodule

// RF
module Register_File (
  input  [31:0] valE,
  input  [31:0] valM,
  input  clk,
  input  [3:0] srcA,
  input  [3:0] srcB,
  input  [3:0] dstE,
  input  [3:0] dstM,
  output [31:0] valA,
  output [31:0] valB,
  output [31:0] eax,
  output [31:0] ecx,
  output [31:0] edx,
  output [31:0] ebx,
  output [31:0] esp,
  output [31:0] ebp,
  output [31:0] esi,
  output [31:0] edi
);

  wire decoder_1_out0, decoder_1_out1, decoder_1_out2, decoder_1_out3, decoder_1_out4, decoder_1_out5,
       decoder_1_out6, decoder_1_out7, decoder_2_out0, decoder_2_out1, decoder_2_out2, decoder_2_out3,
       decoder_2_out4, decoder_2_out5, decoder_2_out6, decoder_2_out7, not_1_out, not_2_out;

  Decoder #(.select(3), .disabled(0)) decoder_1 (
    .out0(decoder_1_out0), .out1(decoder_1_out1), .out2(decoder_1_out2), .out3(decoder_1_out3),
    .out4(decoder_1_out4), .out5(decoder_1_out5), .out6(decoder_1_out6), .out7(decoder_1_out7),
    .sel(dstE[2:0]), .en(not_1_out));
  not not_1 (not_1_out, dstE[3]);
  Decoder #(.select(3), .disabled(0)) decoder_2 (
    .out0(decoder_2_out0), .out1(decoder_2_out1), .out2(decoder_2_out2), .out3(decoder_2_out3),
    .out4(decoder_2_out4), .out5(decoder_2_out5), .out6(decoder_2_out6), .out7(decoder_2_out7),
    .sel(dstM[2:0]), .en(not_2_out));
  not not_2 (not_2_out, dstM[3]);
  _8_Input_Read_Buffer u_8_input_read_buffer_1 (
    .valR(valA), .r0(eax), .r1(ecx), .r2(edx), .r3(ebx), .r4(esp), .r5(ebp), .r6(esi), .r7(edi), .src(srcA));
  _2_Write_Register u_2_write_register_1 (
    .ValM(valM), .ValE(valE), .EnableM(decoder_2_out0), .EnableE(decoder_1_out0), .Clk(clk), .valR(eax));
  _2_Write_Register u_2_write_register_2 (
    .ValM(valM), .ValE(valE), .EnableM(decoder_2_out1), .EnableE(decoder_1_out1), .Clk(clk), .valR(ecx));
  _2_Write_Register u_2_write_register_3 (
    .ValM(valM), .ValE(valE), .EnableM(decoder_2_out2), .EnableE(decoder_1_out2), .Clk(clk), .valR(edx));
  _2_Write_Register u_2_write_register_4 (
    .ValM(valM), .ValE(valE), .EnableM(decoder_2_out3), .EnableE(decoder_1_out3), .Clk(clk), .valR(ebx));
  _2_Write_Register u_2_write_register_5 (
    .ValM(valM), .ValE(valE), .EnableM(decoder_2_out4), .EnableE(decoder_1_out4), .Clk(clk), .valR(esp));
  _2_Write_Register u_2_write_register_6 (
    .ValM(valM), .ValE(valE), .EnableM(decoder_2_out5), .EnableE(decoder_1_out5), .Clk(clk), .valR(ebp));
  _2_Write_Register u_2_write_register_7 (
    .ValM(valM), .ValE(valE), .EnableM(decoder_2_out6), .EnableE(decoder_1_out6), .Clk(clk), .valR(esi));
  _2_Write_Register u_2_write_register_8 (
    .ValM(valM), .ValE(valE), .EnableM(decoder_2_out7), .EnableE(decoder_1_out7), .Clk(clk), .valR(edi));
  _8_Input_Read_Buffer u_8_input_read_buffer_2 (
    .valR(valB), .r0(eax), .r1(ecx), .r2(edx), .r3(ebx), .r4(esp), .r5(ebp), .r6(esi), .r7(edi), .src(srcB));
endmodule

// Read Buf
module _8_Input_Read_Buffer (
  input  [31:0] r0,
  input  [31:0] r1,
  input  [31:0] r2,
  input  [31:0] r3,
  input  [31:0] r4,
  input  [31:0] r5,
  input  [31:0] r6,
  input  [31:0] r7,
  input  [3:0] src,
  output [31:0] valR
);

  wire decoder_1_out0, decoder_1_out1, decoder_1_out2, decoder_1_out3, decoder_1_out4, decoder_1_out5,
       decoder_1_out6, decoder_1_out7;

  assign valR = decoder_1_out0 ? r0 : 32'bz;  // Controlled_Buffer controlled_buffer_1
  assign valR = decoder_1_out1 ? r1 : 32'bz;  // Controlled_Buffer controlled_buffer_2
  assign valR = decoder_1_out2 ? r2 : 32'bz;  // Controlled_Buffer controlled_buffer_3
  assign valR = decoder_1_out3 ? r3 : 32'bz;  // Controlled_Buffer controlled_buffer_4
  assign valR = decoder_1_out4 ? r4 : 32'bz;  // Controlled_Buffer controlled_buffer_5
  assign valR = decoder_1_out5 ? r5 : 32'bz;  // Controlled_Buffer controlled_buffer_6
  assign valR = decoder_1_out6 ? r6 : 32'bz;  // Controlled_Buffer controlled_buffer_7
  assign valR = decoder_1_out7 ? r7 : 32'bz;  // Controlled_Buffer controlled_buffer_8
  Decoder #(.select(3), .disabled(0), .enable("false")) decoder_1 (
    .out0(decoder_1_out0), .out1(decoder_1_out1), .out2(decoder_1_out2), .out3(decoder_1_out3),
    .out4(decoder_1_out4), .out5(decoder_1_out5), .out6(decoder_1_out6), .out7(decoder_1_out7), .sel(src[2:0]));
endmodule

// Reg
module _2_Write_Register (
  input  [31:0] ValM,
  input  [31:0] ValE,
  input  EnableM,
  input  EnableE,
  input  Clk,
  output [31:0] valR
);

  wire xor_1_out;
  wire [31:0] multiplexer_1_out;

  xor xor_1 (xor_1_out, EnableM, EnableE);
  Multiplexer #(.width(32), .disabled(0)) multiplexer_1 (
    .in0(ValM), .in1(ValE), .out(multiplexer_1_out), .sel(EnableE), .en(xor_1_out));
  Register #(.width(32)) register_1 (.D(multiplexer_1_out), .en(xor_1_out), .Q(valR), .clk(Clk));  // open: clr
endmodule

module ID_EX (
  input  cntIsFive,
  input  bubble,
  input  clk,
  input  [3:0] icode,
  input  [3:0] ifun,
  input  [31:0] valC,
  input  [31:0] valA,
  input  [31:0] valB,
  input  [3:0] dstE,
  input  [3:0] dstM,
  output [3:0] icode_2,
  output [3:0] ifun_2,
  output [31:0] valC_2,
  output [31:0] valA_2,
  output [31:0] valB_2,
  output [3:0] dstE_2,
  output [3:0] dstM_2
);

  wire [3:0] multiplexer_1_out, multiplexer_2_out, multiplexer_3_out, multiplexer_4_out, register_1_q,
       register_3_q, register_11_q, register_13_q;
  wire [31:0] register_5_q, register_7_q, register_9_q;

  Multiplexer #(.width(4), .enable("false")) multiplexer_1 (
    .in0(icode), .in1(4'b0001), .out(multiplexer_1_out), .sel(bubble));
  Register #(.width(4)) register_1 (.D(multiplexer_1_out), .Q(register_1_q), .clk(clk));  // open: en, clr
  Register #(.width(4), .trigger("falling")) register_2 (
    .D(register_1_q), .Q(icode_2), .clk(cntIsFive));  // open: en, clr
  Multiplexer #(.width(4), .enable("false")) multiplexer_2 (
    .in0(ifun), .in1(4'b0001), .out(multiplexer_2_out), .sel(bubble));
  Register #(.width(4)) register_3 (.D(multiplexer_2_out), .Q(register_3_q), .clk(clk));  // open: en, clr
  Register #(.width(4), .trigger("falling")) register_4 (
    .D(register_3_q), .Q(ifun_2), .clk(cntIsFive));  // open: en, clr
  Register #(.width(32)) register_5 (.D(valC), .Q(register_5_q), .clk(clk));  // open: en, clr
  Register #(.width(32), .trigger("falling")) register_6 (
    .D(register_5_q), .Q(valC_2), .clk(cntIsFive));  // open: en, clr
  Register #(.width(32)) register_7 (.D(valA), .Q(register_7_q), .clk(clk));  // open: en, clr
  Register #(.width(32), .trigger("falling")) register_8 (
    .D(register_7_q), .Q(valA_2), .clk(cntIsFive));  // open: en, clr
  Register #(.width(32)) register_9 (.D(valB), .Q(register_9_q), .clk(clk));  // open: en, clr
  Register #(.width(32), .trigger("falling")) register_10 (
    .D(register_9_q), .Q(valB_2), .clk(cntIsFive));  // open: en, clr
  Register #(.width(4)) register_11 (.D(multiplexer_3_out), .Q(register_11_q), .clk(clk));  // open: en, clr
  Multiplexer #(.width(4), .enable("false")) multiplexer_3 (
    .in0(dstE), .in1(4'b1111), .out(multiplexer_3_out), .sel(bubble));
  Register #(.width(4), .trigger("falling")) register_12 (
    .D(register_11_q), .Q(dstE_2), .clk(cntIsFive));  // open: en, clr
  Multiplexer #(.width(4), .enable("false")) multiplexer_4 (
    .in0(dstM), .in1(4'b1111), .out(multiplexer_4_out), .sel(bubble));
  Register #(.width(4)) register_13 (.D(multiplexer_4_out), .Q(register_13_q), .clk(clk));  // open: en, clr
  Register #(.width(4), .trigger("falling")) register_14 (
    .D(register_13_q), .Q(dstM_2), .clk(cntIsFive));  // open: en, clr
endmodule

module ALU (
  input  [31:0] valA,
  input  [31:0] valB,
  input  [3:0] ifun,
  input  isOp,
  output [31:0] valE,
  output [2:0] Flgs
);

  wire and_1_out, and_2_out, and_3_out, and_4_out, and_5_out, and_7_out, nor_2_out, not_1_out, or_1_out,
       xnor_1_out;
  wire [1:0] multiplexer_3_out;
  wire [31:0] and_6_out, multiplexer_1_out, multiplexer_2_out, not_2_out, xor_1_out;

  not not_1 (not_1_out, and_7_out);
  assign Flgs[2] = not_1_out ? or_1_out : 1'bz;  // Controlled_Buffer controlled_buffer_1
  and and_1 (and_1_out, xnor_1_out, nor_2_out);
  assign Flgs[2] = and_7_out ? and_1_out : 1'bz;  // Controlled_Buffer controlled_buffer_2
  nor nor_1 (Flgs[1], valE[0], valE[1], valE[2], valE[3], valE[4], valE[5], valE[6], valE[7], valE[8], valE[9], valE[10], valE[11], valE[12], valE[13], valE[14], valE[15], valE[17], valE[18], valE[19], valE[20], valE[21], valE[22], valE[23], valE[24], valE[25], valE[26], valE[27], valE[28], valE[29], valE[30], Flgs[0], valE[16]);
  and and_2 (and_2_out, Flgs[0], and_4_out);
  or or_1 (or_1_out, and_2_out, and_3_out);
  and and_3 (and_3_out, ~Flgs[0], and_5_out);  // AND_Gate
  xnor xnor_1 (xnor_1_out, Flgs[0], valA[31]);
  nor nor_2 (nor_2_out, and_5_out, and_4_out);
  and and_4 (and_4_out, ~valB[31], ~valA[31]);  // AND_Gate
  and and_5 (and_5_out, valB[31], valA[31]);
  assign not_2_out = ~valA;  // NOT_Gate not_2, 32 bits wide
  Multiplexer #(.select(2), .width(32), .enable("false")) multiplexer_1 (
    .in0(valA), .in1(not_2_out), .in2(and_6_out), .in3(xor_1_out), .out(multiplexer_1_out),
    .sel(multiplexer_3_out));
  assign xor_1_out = valA ^ valB;  // XOR_Gate xor_1, 32 bits wide
  assign and_6_out = valA & valB;  // AND_Gate and_6, 32 bits wide
  Adder #(.width(32)) adder_1 (
    .a(multiplexer_2_out), .b(multiplexer_1_out), .out({Flgs[0], valE[30:0]}), .cin(and_7_out));  // open: cout
  Multiplexer #(.select(2), .width(32), .enable("false")) multiplexer_2 (
    .in0(valB), .in1(valB), .in2({32{1'b0}}), .in3({32{1'b0}}), .out(multiplexer_2_out),
    .sel(multiplexer_3_out));
  and and_7 (and_7_out, ~multiplexer_3_out[1], multiplexer_3_out[0]);  // AND_Gate
  Multiplexer #(.width(2), .enable("false")) multiplexer_3 (
    .in0(2'b00), .in1(ifun[1:0]), .out(multiplexer_3_out), .sel(isOp));

  assign valE[31] = Flgs[0];
endmodule

module ALU_A (
  input  [31:0] valA,
  input  [31:0] valC,
  input  [3:0] icode,
  output [31:0] ALU_A
);

  wire nand_1_out;
  wire [0:0] multiplexer_1_out;

  Multiplexer #(.enable("false")) multiplexer_1 (
    .in0(nand_1_out), .in1(icode[0]), .out(multiplexer_1_out[0]), .sel(icode[3]));
  nand nand_1 (nand_1_out, icode[1], ~icode[0]);  // NAND_Gate
  Multiplexer #(.select(2), .width(32), .enable("false")) multiplexer_2 (
    .in0(valA), .in1(valC), .in2(32'hfffffffc), .in3(32'h4), .out(ALU_A),
    .sel({icode[3], multiplexer_1_out[0]}));
endmodule

module ALU_B (
  input  [31:0] valB,
  input  [3:0] icode,
  output [31:0] ALU_B
);

  wire or_1_out;

  or or_1 (or_1_out, icode[3], icode[2]);
  Multiplexer #(.width(32), .enable("false")) multiplexer_1 (.in0({32{1'b0}}), .in1(valB), .out(ALU_B), .sel(or_1_out));
endmodule

module Cnd (
  input  [3:0] ifun,
  input  [2:0] Flgs,
  output Cnd
);

  wire and_1_out, and_2_out, not_1_out, not_2_out, or_1_out, xor_1_out;

  or or_1 (or_1_out, xor_1_out, and_2_out);
  xor xor_1 (xor_1_out, Flgs[0], Flgs[2]);
  Multiplexer #(.select(3), .enable("false")) multiplexer_1 (
    .in0(1'b1), .in1(or_1_out), .in2(xor_1_out), .in3(and_2_out), .in4(not_1_out), .in5(not_2_out),
    .in6(and_1_out), .out(Cnd), .sel(ifun[2:0]));  // open: in7
  not not_1 (not_1_out, and_2_out);
  and and_1 (and_1_out, not_2_out, ~and_2_out);  // AND_Gate
  not not_2 (not_2_out, xor_1_out);
  and and_2 (and_2_out, Flgs[1], ~Flgs[2]);  // AND_Gate
endmodule

module CC (
  input  [2:0] Flgs,
  input  Clk,
  input  En,
  output [2:0] Flgs_2
);

  Register #(.width(1)) Signed (.D(Flgs[0]), .en(En), .Q(Flgs_2[0]), .clk(Clk));  // open: clr
  Register #(.width(1)) Zero (.D(Flgs[1]), .en(En), .Q(Flgs_2[1]), .clk(Clk));  // open: clr
  Register #(.width(1)) Overflow (.D(Flgs[2]), .en(En), .Q(Flgs_2[2]), .clk(Clk));  // open: clr
endmodule

// En
module CCEn (
  input  [3:0] icode,
  output CCEn
);

  and and_1 (CCEn, ~icode[3], icode[2], icode[1], ~icode[0]);  // AND_Gate
endmodule

// cmov
module cmov_Addr_Handler (
  input  [3:0] icode,
  input  Cnd,
  input  [3:0] dstE,
  output [3:0] dstE_2
);

  wire nor_1_out;

  Multiplexer #(.width(4), .enable("false")) multiplexer_1 (.in0(dstE), .in1(4'b1111), .out(dstE_2), .sel(nor_1_out));
  nor nor_1 (nor_1_out, icode[0], ~icode[1], icode[2], icode[3], Cnd);  // NOR_Gate
endmodule

module EX_MEM (
  input  cntIsFive,
  input  clk,
  input  [3:0] icode,
  input  Cnd,
  input  [31:0] valE,
  input  [31:0] valA,
  input  [3:0] dstE,
  input  [3:0] dstM,
  output [3:0] icode_2,
  output Cnd_2,
  output [31:0] valE_2,
  output [31:0] valA_2,
  output [3:0] dstE_2,
  output [3:0] dstM_2
);

  wire register_3_q;
  wire [3:0] register_1_q, register_9_q, register_11_q;
  wire [31:0] register_6_q, register_7_q;

  Register #(.width(4)) register_1 (.D(icode), .Q(register_1_q), .clk(clk));  // open: en, clr
  Register #(.width(4)) register_2 (.D(register_1_q), .en(cntIsFive), .Q(icode_2), .clk(clk));  // open: clr
  Register #(.width(1)) register_3 (.D(Cnd), .Q(register_3_q), .clk(clk));  // open: en, clr
  Register #(.width(1)) register_4 (.D(register_3_q), .en(cntIsFive), .Q(Cnd_2), .clk(clk));  // open: clr
  Register #(.width(32)) register_5 (.D(register_6_q), .en(cntIsFive), .Q(valE_2), .clk(clk));  // open: clr
  Register #(.width(32)) register_6 (.D(valE), .Q(register_6_q), .clk(clk));  // open: en, clr
  Register #(.width(32)) register_7 (.D(valA), .Q(register_7_q), .clk(clk));  // open: en, clr
  Register #(.width(32)) register_8 (.D(register_7_q), .en(cntIsFive), .Q(valA_2), .clk(clk));  // open: clr
  Register #(.width(4)) register_9 (.D(dstE), .Q(register_9_q), .clk(clk));  // open: en, clr
  Register #(.width(4)) register_10 (.D(register_9_q), .en(cntIsFive), .Q(dstE_2), .clk(clk));  // open: clr
  Register #(.width(4)) register_11 (.D(dstM), .Q(register_11_q), .clk(clk));  // open: en, clr
  Register #(.width(4)) register_12 (.D(register_11_q), .en(cntIsFive), .Q(dstM_2), .clk(clk));  // open: clr
endmodule

module Data_Memory (
  input  write,
  input  read,
  input  clk,
  input  [3:0] count,
  input  [31:0] valAddr,
  input  [31:0] valA,
  output [31:0] valM
);

  wire and_1_out, not_1_out, or_1_out;
  wire [7:0] multiplexer_1_out, ram_1_data;
  wire [23:0] adder_1_out, bit_extender_1_out;

  or or_1 (or_1_out, write, read);
  assign bit_extender_1_out = {{22{1'b0}}, count[1:0]};  // Bit_Extender bit_extender_1
  and and_1 (and_1_out, or_1_out, ~count[2]);  // AND_Gate
  Adder #(.width(24)) adder_1 (.a(bit_extender_1_out), .b(valAddr[23:0]), .out(adder_1_out));  // open: cin, cout
  _4x8_RFile u_4x8_rfile_1 (
    .En(1'b1), .Address(count[1:0]), .I_DATA(ram_1_data), .CLK(clk), .Bits_0_7(valM[7:0]),
    .Bits_8_15(valM[15:8]), .Bits_16_23(valM[23:16]), .Bits_24_31(valM[31:24]));
  RAM #(.addrWidth(24)) ram_1 (
    .addr(adder_1_out), .data(ram_1_data), .sel(and_1_out), .clk(clk), .ld(read));  // open: clr
  assign ram_1_data = not_1_out ? multiplexer_1_out : 8'bz;  // Controlled_Buffer controlled_buffer_1
  not not_1 (not_1_out, read);
  Multiplexer #(.select(2), .width(8), .enable("false")) multiplexer_1 (
    .in0(valA[7:0]), .in1(valA[15:8]), .in2(valA[23:16]), .in3(valA[31:24]), .out(multiplexer_1_out),
    .sel(count[1:0]));
endmodule

// Addr
module Mem_Addr (
  input  [3:0] icode,
  input  [31:0] valE,
  input  [31:0] valA,
  output [31:0] valAddr
);

  wire and_1_out;

  and and_1 (and_1_out, icode[0], icode[3]);
  Multiplexer #(.width(32), .enable("false")) multiplexer_1 (.in0(valE), .in1(valA), .out(valAddr), .sel(and_1_out));
endmodule

// WR Sig
module Mem__Sig (
  input  [3:0] icode,
  output Write,
  output Read
);

  wire and_1_out, or_1_out;

  and and_1 (and_1_out, ~icode[1], icode[2]);  // AND_Gate
  or or_1 (or_1_out, and_1_out, icode[3]);
  Demultiplexer #(.disabled(0), .enable("false")) demultiplexer_1 (
    .out0(Write), .out1(Read), .in(or_1_out), .sel(icode[0]));
endmodule

module MEM_WBN (
  input  cntIsFive,
  input  clk,
  input  [3:0] icode,
  input  [31:0] valE,
  input  [31:0] valM,
  input  [3:0] dstE,
  input  [3:0] dstM,
  output [3:0] icode_2,
  output [31:0] valE_2,
  output [31:0] valM_2,
  output [3:0] dstE_2,
  output [3:0] dstM_2
);

  wire [3:0] register_1_q, register_8_q, register_9_q;
  wire [31:0] register_3_q, register_5_q;

  Register #(.width(4)) register_1 (.D(icode), .Q(register_1_q), .clk(clk));  // open: en, clr
  Register #(.width(4)) register_2 (.D(register_1_q), .en(cntIsFive), .Q(icode_2), .clk(clk));  // open: clr
  Register #(.width(32)) register_3 (.D(valE), .Q(register_3_q), .clk(clk));  // open: en, clr
  Register #(.width(32)) register_4 (.D(register_3_q), .en(cntIsFive), .Q(valE_2), .clk(clk));  // open: clr
  Register #(.width(32)) register_5 (.D(valM), .Q(register_5_q), .clk(clk));  // open: en, clr
  Register #(.width(32)) register_6 (.D(register_5_q), .en(cntIsFive), .Q(valM_2), .clk(clk));  // open: clr
  Register #(.width(4)) register_7 (.D(register_8_q), .en(cntIsFive), .Q(dstE_2), .clk(clk));  // open: clr
  Register #(.width(4)) register_8 (.D(dstE), .Q(register_8_q), .clk(clk));  // open: en, clr
  Register #(.width(4)) register_9 (.D(dstM), .Q(register_9_q), .clk(clk));  // open: en, clr
  Register #(.width(4)) register_10 (.D(register_9_q), .en(cntIsFive), .Q(dstM_2), .clk(clk));  // open: clr
endmodule

// Hazard Controller
module Control_Hazard_Handler (
  input  [3:0] M_icode,
  input  E_Cnd,
  input  [3:0] E_icode,
  input  [3:0] E_dstM,
  input  [3:0] D_icode,
  input  [3:0] srcB,
  input  [3:0] srcA,
  output E_bubble,
  output D_stall,
  output D_bubble,
  output F_stall
);

  wire and_1_out, and_2_out, and_4_out, and_5_out, and_6_out, and_7_out, and_8_out, and_9_out, and_10_out,
       or_1_out, or_2_out, or_4_out, xor_1_out, xor_2_out;
  wire [2:0] xnor_1_out, xnor_2_out;

  and and_1 (and_1_out, and_2_out, ~E_Cnd);  // AND_Gate
  or or_1 (or_1_out, and_8_out, and_9_out, and_10_out);
  and and_2 (and_2_out, and_4_out, ~E_icode[3]);  // AND_Gate
  and and_3 (D_stall, and_7_out, or_2_out);
  and and_4 (and_4_out, E_icode[0], E_icode[1], E_icode[2]);
  or or_2 (or_2_out, and_5_out, and_6_out);
  and and_5 (and_5_out, xnor_1_out[0], xnor_1_out[1], xnor_1_out[2], ~srcB[3], ~E_dstM[3]);  // AND_Gate
  and and_6 (and_6_out, xnor_2_out[0], xnor_2_out[1], xnor_2_out[2], ~E_dstM[3], ~srcA[3]);  // AND_Gate
  and and_7 (and_7_out, E_icode[0], xor_1_out, xor_2_out);
  assign xnor_1_out = ~(E_dstM[2:0] ^ srcB[2:0]);  // XNOR_Gate xnor_1, 3 bits wide
  assign xnor_2_out = ~(E_dstM[2:0] ^ srcA[2:0]);  // XNOR_Gate xnor_2, 3 bits wide
  and and_8 (and_8_out, M_icode[0], ~M_icode[1], ~M_icode[2], M_icode[3]);  // AND_Gate
  and and_9 (and_9_out, E_icode[0], ~E_icode[1], ~E_icode[2], E_icode[3]);  // AND_Gate
  xor xor_1 (xor_1_out, E_icode[1], E_icode[2]);
  xor xor_2 (xor_2_out, E_icode[2], E_icode[3]);
  or or_3 (E_bubble, and_1_out, D_stall);
  and and_10 (and_10_out, D_icode[0], ~D_icode[1], ~D_icode[2], D_icode[3]);  // AND_Gate
  or or_4 (or_4_out, and_10_out, or_1_out, and_1_out);
  or or_5 (F_stall, D_stall, or_1_out);
  and and_11 (D_bubble, ~D_stall, or_4_out);  // AND_Gate
endmodule

module Halt (
  input  [3:0] icode,
  input  cntIsZero,
  output halt,
  output [3:0] icode_2
);

  wire and_1_out, nor_1_out;
  wire [2:0] counter_1_q;

  nor nor_1 (nor_1_out, icode[3], icode[2], icode[1], icode[0]);
  Counter #(.width(3), .max('h7)) counter_1 (.Q(counter_1_q), .clk(and_1_out));  // open: load, D, count, carry, clr
  and and_1 (and_1_out, nor_1_out, cntIsZero);
  and and_2 (halt, counter_1_q[2], counter_1_q[0]);

  assign icode_2 = icode;
endmodule
